// Logisim project 32 Bit RiscV.circ as structural Verilog: 17 circuits, main circuit Decode
module Decode (
  input  [31:0] instruction_In,
  output [31:0] _0_31,
  output [4:0] _32_36
);

  wire not_1_out, not_2_out, not_3_out, not_4_out, not_5_out, not_6_out, not_7_out, not_8_out, not_9_out;

  not not_1 (not_1_out, instruction_In[30]);
  not not_2 (not_2_out, instruction_In[14]);
  not not_3 (not_3_out, instruction_In[13]);
  not not_4 (not_4_out, instruction_In[12]);
  not not_5 (not_5_out, instruction_In[6]);
  not not_6 (not_6_out, instruction_In[5]);
  not not_7 (not_7_out, instruction_In[4]);
  not not_8 (not_8_out, instruction_In[3]);
  not not_9 (not_9_out, instruction_In[2]);
  and ADD (_0_31[0], instruction_In[0], instruction_In[1], not_9_out, not_8_out, instruction_In[4], instruction_In[5], not_5_out, not_4_out, not_3_out, not_2_out, not_1_out);
  and SUB (_0_31[1], instruction_In[0], instruction_In[1], not_9_out, not_8_out, instruction_In[4], instruction_In[5], not_5_out, not_4_out, not_3_out, not_2_out, instruction_In[30]);
  and XOR (_0_31[2], instruction_In[0], instruction_In[1], not_9_out, not_8_out, instruction_In[4], instruction_In[5], not_5_out, not_4_out, not_3_out, instruction_In[14], not_1_out);
  and OR (_0_31[3], instruction_In[0], instruction_In[1], not_9_out, not_8_out, instruction_In[4], instruction_In[5], not_5_out, not_4_out, instruction_In[13], instruction_In[14], not_1_out);
  and AND (_0_31[4], instruction_In[0], instruction_In[1], not_9_out, not_8_out, instruction_In[4], instruction_In[5], not_5_out, instruction_In[12], instruction_In[13], instruction_In[14], not_1_out);
  and sll (_0_31[5], instruction_In[0], instruction_In[1], not_9_out, not_8_out, instruction_In[4], instruction_In[5], not_5_out, instruction_In[12], not_3_out, not_2_out, not_1_out);
  and srl (_0_31[6], instruction_In[0], instruction_In[1], not_9_out, not_8_out, instruction_In[4], instruction_In[5], not_5_out, instruction_In[12], instruction_In[13], not_2_out, not_1_out);
  and sra (_0_31[7], instruction_In[0], instruction_In[1], not_9_out, not_8_out, instruction_In[4], instruction_In[5], not_5_out, instruction_In[12], instruction_In[13], not_2_out, instruction_In[30]);
  and slt (_0_31[8], instruction_In[0], instruction_In[1], not_9_out, not_8_out, instruction_In[4], instruction_In[5], not_5_out, not_4_out, instruction_In[13], not_2_out, not_1_out);
  and sltu (_0_31[9], instruction_In[0], instruction_In[1], not_9_out, not_8_out, instruction_In[4], instruction_In[5], not_5_out, instruction_In[12], instruction_In[13], not_2_out, not_1_out);
  and addi (_0_31[10], instruction_In[0], instruction_In[1], not_9_out, not_8_out, instruction_In[4], not_6_out, not_5_out, not_4_out, not_3_out, not_2_out);
  and xori (_0_31[11], instruction_In[0], instruction_In[1], not_9_out, not_8_out, instruction_In[4], not_6_out, not_5_out, not_4_out, not_3_out, instruction_In[14]);
  and ori (_0_31[12], instruction_In[0], instruction_In[1], not_9_out, not_8_out, instruction_In[4], not_6_out, not_5_out, not_4_out, not_3_out, instruction_In[14]);
  and andi (_0_31[13], instruction_In[0], instruction_In[1], not_9_out, not_8_out, instruction_In[4], not_6_out, not_5_out, instruction_In[12], instruction_In[13], instruction_In[14]);
  and slli (_0_31[14], instruction_In[0], instruction_In[1], not_9_out, not_8_out, instruction_In[4], not_6_out, not_5_out, instruction_In[12], not_3_out, not_2_out, not_1_out);
  and srli (_0_31[15], instruction_In[0], instruction_In[1], not_9_out, not_8_out, instruction_In[4], not_6_out, not_5_out, instruction_In[12], not_3_out, instruction_In[14], not_1_out);
  and srai (_0_31[16], instruction_In[0], instruction_In[1], not_9_out, not_8_out, instruction_In[4], not_6_out, not_5_out, instruction_In[12], not_3_out, instruction_In[14], instruction_In[30]);
  and slti (_0_31[17], instruction_In[0], instruction_In[1], not_9_out, not_8_out, instruction_In[4], not_6_out, not_5_out, not_4_out, instruction_In[13], not_2_out);
  and sltiu (_0_31[18], instruction_In[0], instruction_In[1], not_9_out, not_8_out, instruction_In[4], not_6_out, not_5_out, instruction_In[12], instruction_In[13], not_2_out);
  and lb (_0_31[19], instruction_In[0], instruction_In[1], not_9_out, not_8_out, not_7_out, not_6_out, not_5_out, not_4_out, not_3_out, not_2_out);
  and lh (_0_31[20], instruction_In[0], instruction_In[1], not_9_out, not_8_out, not_7_out, not_6_out, not_5_out, instruction_In[12], not_3_out, not_2_out);
  and lw (_0_31[21], instruction_In[0], instruction_In[1], not_9_out, not_8_out, not_7_out, not_6_out, not_5_out, not_4_out, instruction_In[13], not_2_out);
  and lbu (_0_31[22], instruction_In[0], instruction_In[1], not_9_out, not_8_out, not_7_out, not_6_out, not_5_out, not_4_out, not_3_out, instruction_In[14]);
  and lhu (_0_31[23], instruction_In[0], instruction_In[1], not_9_out, not_8_out, not_7_out, not_6_out, not_5_out, instruction_In[12], not_3_out, instruction_In[14]);
  and sb (_0_31[24], instruction_In[0], instruction_In[1], not_9_out, not_8_out, not_7_out, instruction_In[5], not_5_out, not_4_out, not_3_out, not_2_out);
  and sh (_0_31[25], instruction_In[0], instruction_In[1], not_9_out, not_8_out, not_7_out, instruction_In[5], not_5_out, instruction_In[12], not_3_out, not_2_out);
  and sw (_0_31[26], instruction_In[0], instruction_In[1], not_9_out, not_8_out, not_7_out, instruction_In[5], not_5_out, not_4_out, instruction_In[13], not_2_out);
  and beq (_0_31[27], instruction_In[0], instruction_In[1], not_9_out, not_8_out, not_7_out, instruction_In[5], instruction_In[6], not_4_out, not_3_out, not_2_out);
  and bne (_0_31[28], instruction_In[0], instruction_In[1], not_9_out, not_8_out, not_7_out, instruction_In[5], instruction_In[6], instruction_In[12], not_3_out, not_2_out);
  and blt (_0_31[29], instruction_In[0], instruction_In[1], not_9_out, not_8_out, not_7_out, instruction_In[5], instruction_In[6], not_4_out, not_3_out, instruction_In[14]);
  and bge (_0_31[30], instruction_In[0], instruction_In[1], not_9_out, not_8_out, not_7_out, instruction_In[5], instruction_In[6], instruction_In[12], not_3_out, instruction_In[14]);
  and bltu (_0_31[31], instruction_In[0], instruction_In[1], not_9_out, not_8_out, not_7_out, instruction_In[5], instruction_In[6], not_4_out, instruction_In[13], instruction_In[14]);
  and bgeu (_32_36[0], instruction_In[0], instruction_In[1], not_9_out, not_8_out, not_7_out, instruction_In[5], instruction_In[6], instruction_In[12], instruction_In[13], instruction_In[14]);
  and jal (_32_36[1], instruction_In[0], instruction_In[1], instruction_In[2], instruction_In[3], not_7_out, instruction_In[5], instruction_In[6]);
  and jalr (_32_36[2], instruction_In[0], instruction_In[1], instruction_In[2], not_8_out, not_7_out, instruction_In[5], instruction_In[6], not_4_out, not_3_out, not_2_out);
  and lui (_32_36[3], instruction_In[0], instruction_In[1], instruction_In[2], not_8_out, instruction_In[4], instruction_In[5], not_5_out);
  and auipc (_32_36[4], instruction_In[0], instruction_In[1], instruction_In[2], not_8_out, instruction_In[4], not_6_out, not_5_out);
endmodule

module Register_File (
  input  CLK,
  input  [31:0] Data_In,
  input  WE,
  input  [4:0] rs1,
  input  [4:0] Select,
  input  [4:0] rs2,
  input  CLR,
  output [31:0] rs1_out,
  output [31:0] rs2_out
);

  wire demultiplexer_1_out0, demultiplexer_1_out1, demultiplexer_1_out2, demultiplexer_1_out3,
       demultiplexer_1_out4, demultiplexer_1_out5, demultiplexer_1_out6, demultiplexer_1_out7,
       demultiplexer_1_out8, demultiplexer_1_out9, demultiplexer_1_out10, demultiplexer_1_out11,
       demultiplexer_1_out12, demultiplexer_1_out13, demultiplexer_1_out14, demultiplexer_1_out15,
       demultiplexer_1_out16, demultiplexer_1_out17, demultiplexer_1_out18, demultiplexer_1_out19,
       demultiplexer_1_out20, demultiplexer_1_out21, demultiplexer_1_out22, demultiplexer_1_out23,
       demultiplexer_1_out24, demultiplexer_1_out25, demultiplexer_1_out26, demultiplexer_1_out27,
       demultiplexer_1_out28, demultiplexer_1_out29, demultiplexer_1_out30, demultiplexer_1_out31;
  wire [31:0] undriven, x0_q, x1_q, x2_q, x3_q, x4_q, x5_q, x6_q, x7_q, x8_q, x9_q, x10_q, x11_q, x12_q,
       x13_q, x14_q, x15_q, x16_q, x17_q, x18_q, x19_q, x20_q, x21_q, x22_q, x23_q, x24_q, x25_q, x26_q,
       x27_q, x28_q, x29_q, x30_q, x31_q;

  Demultiplexer #(.enable("false"), .select(5)) demultiplexer_1 (
    .out0(demultiplexer_1_out0), .out1(demultiplexer_1_out1), .out2(demultiplexer_1_out2),
    .out3(demultiplexer_1_out3), .out4(demultiplexer_1_out4), .out5(demultiplexer_1_out5),
    .out6(demultiplexer_1_out6), .out7(demultiplexer_1_out7), .out8(demultiplexer_1_out8),
    .out9(demultiplexer_1_out9), .out10(demultiplexer_1_out10), .out11(demultiplexer_1_out11),
    .out12(demultiplexer_1_out12), .out13(demultiplexer_1_out13), .out14(demultiplexer_1_out14),
    .out15(demultiplexer_1_out15), .out16(demultiplexer_1_out16), .out17(demultiplexer_1_out17),
    .out18(demultiplexer_1_out18), .out19(demultiplexer_1_out19), .out20(demultiplexer_1_out20),
    .out21(demultiplexer_1_out21), .out22(demultiplexer_1_out22), .out23(demultiplexer_1_out23),
    .out24(demultiplexer_1_out24), .out25(demultiplexer_1_out25), .out26(demultiplexer_1_out26),
    .out27(demultiplexer_1_out27), .out28(demultiplexer_1_out28), .out29(demultiplexer_1_out29),
    .out30(demultiplexer_1_out30), .out31(demultiplexer_1_out31), .in(WE), .sel(Select));
  Register #(.width(32)) x0 (.D(Data_In), .en(demultiplexer_1_out0), .clk(CLK), .Q(x0_q), .clr(CLR));
  Register #(.width(32)) x1 (.D(Data_In), .en(demultiplexer_1_out1), .clk(CLK), .Q(x1_q), .clr(CLR));
  Register #(.width(32)) x2 (.D(Data_In), .en(demultiplexer_1_out2), .clk(CLK), .Q(x2_q), .clr(CLR));
  Register #(.width(32)) x3 (.D(Data_In), .en(demultiplexer_1_out3), .clk(CLK), .Q(x3_q), .clr(CLR));
  Register #(.width(32)) x4 (.D(Data_In), .en(demultiplexer_1_out4), .clk(CLK), .Q(x4_q), .clr(CLR));
  Register #(.width(32)) x5 (.D(Data_In), .en(demultiplexer_1_out5), .clk(CLK), .Q(x5_q), .clr(CLR));
  Register #(.width(32)) x6 (.D(Data_In), .en(demultiplexer_1_out6), .clk(CLK), .Q(x6_q), .clr(CLR));
  Register #(.width(32)) x7 (.D(Data_In), .en(demultiplexer_1_out7), .clk(CLK), .Q(x7_q), .clr(CLR));
  Register #(.width(32)) x8 (.D(Data_In), .en(demultiplexer_1_out8), .clk(CLK), .Q(x8_q), .clr(CLR));
  Register #(.width(32)) x9 (.D(Data_In), .en(demultiplexer_1_out9), .clk(CLK), .Q(x9_q), .clr(CLR));
  Register #(.width(32)) x10 (.D(Data_In), .en(demultiplexer_1_out10), .clk(CLK), .Q(x10_q), .clr(CLR));
  Register #(.width(32)) x11 (.D(Data_In), .en(demultiplexer_1_out11), .clk(CLK), .Q(x11_q), .clr(CLR));
  Register #(.width(32)) x12 (.D(Data_In), .en(demultiplexer_1_out12), .clk(CLK), .Q(x12_q), .clr(CLR));
  Register #(.width(32)) x13 (.D(Data_In), .en(demultiplexer_1_out13), .clk(CLK), .Q(x13_q), .clr(CLR));
  Register #(.width(32)) x14 (.D(Data_In), .en(demultiplexer_1_out14), .clk(CLK), .Q(x14_q), .clr(CLR));
  Register #(.width(32)) x15 (.D(Data_In), .en(demultiplexer_1_out15), .clk(CLK), .Q(x15_q), .clr(CLR));
  Register #(.width(32)) x16 (.D(undriven), .en(demultiplexer_1_out16), .clk(CLK), .Q(x16_q), .clr(CLR));
  Register #(.width(32)) x17 (.D(undriven), .en(demultiplexer_1_out17), .clk(CLK), .Q(x17_q), .clr(CLR));
  Register #(.width(32)) x18 (.D(undriven), .en(demultiplexer_1_out18), .clk(CLK), .Q(x18_q), .clr(CLR));
  Register #(.width(32)) x19 (.D(undriven), .en(demultiplexer_1_out19), .clk(CLK), .Q(x19_q), .clr(CLR));
  Register #(.width(32)) x20 (.D(undriven), .en(demultiplexer_1_out20), .clk(CLK), .Q(x20_q), .clr(CLR));
  Register #(.width(32)) x21 (.D(undriven), .en(demultiplexer_1_out21), .clk(CLK), .Q(x21_q), .clr(CLR));
  Register #(.width(32)) x22 (.D(undriven), .en(demultiplexer_1_out22), .clk(CLK), .Q(x22_q), .clr(CLR));
  Register #(.width(32)) x23 (.D(undriven), .en(demultiplexer_1_out23), .clk(CLK), .Q(x23_q), .clr(CLR));
  Register #(.width(32)) x24 (.D(undriven), .en(demultiplexer_1_out24), .clk(CLK), .Q(x24_q), .clr(CLR));
  Register #(.width(32)) x25 (.D(undriven), .en(demultiplexer_1_out25), .clk(CLK), .Q(x25_q), .clr(CLR));
  Register #(.width(32)) x26 (.D(undriven), .en(demultiplexer_1_out26), .clk(CLK), .Q(x26_q), .clr(CLR));
  Register #(.width(32)) x27 (.D(undriven), .en(demultiplexer_1_out27), .clk(CLK), .Q(x27_q), .clr(CLR));
  Register #(.width(32)) x28 (.D(undriven), .en(demultiplexer_1_out28), .clk(CLK), .Q(x28_q), .clr(CLR));
  Register #(.width(32)) x29 (.D(undriven), .en(demultiplexer_1_out29), .clk(CLK), .Q(x29_q), .clr(CLR));
  Register #(.width(32)) x30 (.D(undriven), .en(demultiplexer_1_out30), .clk(CLK), .Q(x30_q), .clr(CLR));
  Register #(.width(32)) x31 (.D(undriven), .en(demultiplexer_1_out31), .clk(CLK), .Q(x31_q));  // open: clr
  Multiplexer #(.enable("false"), .select(5), .width(32)) multiplexer_1 (
    .in0(x0_q), .in1(x1_q), .in2(x2_q), .in3(x3_q), .in4(x4_q), .in5(x5_q), .in6(x6_q), .in7(x7_q),
    .in8(x8_q), .in9(x9_q), .in10(x10_q), .in11(x11_q), .in12(x12_q), .in13(x13_q), .in14(x14_q),
    .in15(x15_q), .in16(x16_q), .in17(x17_q), .in18(x18_q), .in19(x19_q), .in20(x20_q), .in21(x21_q),
    .in22(x22_q), .in23(x23_q), .in24(x24_q), .in25(x25_q), .in26(x26_q), .in27(x27_q), .in28(x28_q),
    .in29(x29_q), .in30(x30_q), .in31(x31_q), .out(rs1_out), .sel(rs1));
  Multiplexer #(.enable("false"), .select(5), .width(32)) multiplexer_2 (
    .in0(x0_q), .in1(x1_q), .in2(x2_q), .in3(x3_q), .in4(x4_q), .in5(x5_q), .in6(x6_q), .in7(x7_q),
    .in8(x8_q), .in9(x9_q), .in10(x10_q), .in11(x11_q), .in12(x12_q), .in13(x13_q), .in14(x14_q),
    .in15(x15_q), .in16(x16_q), .in17(x17_q), .in18(x18_q), .in19(x19_q), .in20(x20_q), .in21(x21_q),
    .in22(x22_q), .in23(x23_q), .in24(x24_q), .in25(x25_q), .in26(x26_q), .in27(x27_q), .in28(x28_q),
    .in29(x29_q), .in30(x30_q), .in31(x31_q), .out(rs2_out), .sel(rs2));
endmodule

module Program_Counter (
  input  CLR,
  input  CLK,
  input  stall,
  input  [31:0] Data,
  output [31:0] out_5
);

  wire not_1_out;

  not not_1 (not_1_out, stall);
  Register #(.trigger("falling"), .width(32)) register_1 (.D(Data), .en(not_1_out), .clk(CLK), .Q(out_5), .clr(CLR));
endmodule

module Decode_Signals (
  input  [31:0] Instruction,
  output [4:0] rd,
  output [4:0] rs1,
  output [4:0] rs2,
  output [3:0] ALU,
  output immediate_select,
  output Mem_write,
  output [3:0] Branch,
  output Unsigned,
  output WE,
  output ALU_WB,
  output ID_EX_memread,
  output Jump
);

  wire and_1_out, and_2_out, and_3_out, and_4_out, and_5_out, and_6_out, and_7_out, and_8_out, nor_1_out,
       nor_2_out, nor_3_out, nor_4_out, nor_5_out, nor_6_out, nor_7_out, nor_8_out, nor_9_out, nor_10_out,
       nor_11_out, nor_12_out, nor_13_out, nor_14_out, nor_15_out, nor_16_out, nor_17_out, nor_18_out,
       nor_19_out, nor_20_out, nor_21_out, nor_22_out, nor_23_out, or_1_out, or_2_out, or_3_out, or_4_out,
       or_5_out, or_6_out, or_7_out, or_8_out, or_9_out, or_10_out, or_11_out, or_12_out, or_13_out,
       or_17_out, or_18_out, or_19_out;
  wire [4:0] decimal_to_binary_1_binary, decode_1__32_36;
  wire [16:0] decode_1__0_31;
  wire [31:10] decode_1__0_31_2;

  Decode decode_1 (
    .instruction_In(Instruction),
    ._0_31({decode_1__0_31_2[31:29], Branch[1:0], decode_1__0_31[16:10], decode_1__0_31_2[19:10], decode_1__0_31[9:0]}),
    ._32_36(decode_1__32_36));
  and and_1 (and_1_out, Instruction[0], Instruction[1], Instruction[2], ~Instruction[3], ~Instruction[4], Instruction[5], Instruction[6]);  // AND_Gate
  and and_2 (and_2_out, Instruction[0], Instruction[1], ~Instruction[2], ~Instruction[3], Instruction[4], Instruction[5], ~Instruction[6]);  // AND_Gate
  and and_3 (and_3_out, Instruction[0], Instruction[1], ~Instruction[2], ~Instruction[3], Instruction[4], ~Instruction[5], ~Instruction[6]);  // AND_Gate
  and and_4 (and_4_out, Instruction[0], Instruction[1], Instruction[2], ~Instruction[3], Instruction[4], Instruction[5], ~Instruction[6]);  // AND_Gate
  and and_5 (and_5_out, Instruction[0], Instruction[1], Instruction[2], Instruction[3], ~Instruction[4], Instruction[5], Instruction[6]);  // AND_Gate
  and and_6 (and_6_out, Instruction[0], Instruction[1], ~Instruction[2], ~Instruction[3], ~Instruction[4], Instruction[5], ~Instruction[6]);  // AND_Gate
  and and_7 (and_7_out, Instruction[0], Instruction[1], ~Instruction[2], ~Instruction[3], ~Instruction[4], Instruction[5], Instruction[6]);  // AND_Gate
  and and_8 (and_8_out, Instruction[0], Instruction[1], ~Instruction[2], ~Instruction[3], ~Instruction[4], ~Instruction[5], ~Instruction[6]);  // AND_Gate
  nor nor_1 (nor_1_out, decode_1__0_31[0], decode_1__0_31_2[10]);
  nor nor_2 (nor_2_out, decode_1__0_31[2], decode_1__0_31_2[11]);
  or or_1 (or_1_out, decode_1__0_31[3], decode_1__0_31_2[12]);
  nor nor_3 (nor_3_out, decode_1__0_31[4], decode_1__0_31_2[13]);
  nor nor_4 (nor_4_out, decode_1__0_31[5], decode_1__0_31_2[14]);
  or or_2 (or_2_out, decode_1__0_31[6], decode_1__0_31_2[15]);
  nor nor_5 (nor_5_out, decode_1__0_31[7], decode_1__0_31_2[16]);
  nor nor_6 (nor_6_out, decode_1__0_31[8], decode_1__0_31_2[17]);
  or or_3 (or_3_out, decode_1__0_31[9], decode_1__0_31_2[18]);
  nor nor_7 (nor_7_out, decode_1__0_31[0], decode_1__0_31_2[10]);
  or or_4 (or_4_out, decode_1__0_31[2], decode_1__0_31_2[11]);
  nor nor_8 (nor_8_out, decode_1__0_31[3], decode_1__0_31_2[12]);
  nor nor_9 (nor_9_out, decode_1__0_31[4], decode_1__0_31_2[13]);
  or or_5 (or_5_out, decode_1__0_31[5], decode_1__0_31_2[14]);
  or or_6 (or_6_out, decode_1__0_31[6], decode_1__0_31_2[15]);
  or or_7 (or_7_out, decode_1__0_31[7], decode_1__0_31_2[16]);
  nor nor_10 (nor_10_out, decode_1__0_31[8], decode_1__0_31_2[17]);
  nor nor_11 (nor_11_out, decode_1__0_31[9], decode_1__0_31_2[18]);
  nor nor_12 (nor_12_out, decode_1__0_31[0], decode_1__0_31_2[10]);
  or or_8 (or_8_out, decode_1__0_31[2], decode_1__0_31_2[11]);
  or or_9 (or_9_out, decode_1__0_31[3], decode_1__0_31_2[12]);
  or or_10 (or_10_out, decode_1__0_31[4], decode_1__0_31_2[13]);
  nor nor_13 (nor_13_out, decode_1__0_31[5], decode_1__0_31_2[14]);
  nor nor_14 (nor_14_out, decode_1__0_31[6], decode_1__0_31_2[15]);
  nor nor_15 (nor_15_out, decode_1__0_31[7], decode_1__0_31_2[16]);
  nor nor_16 (nor_16_out, decode_1__0_31[8], decode_1__0_31_2[17]);
  nor nor_17 (nor_17_out, decode_1__0_31[9], decode_1__0_31_2[18]);
  nor nor_18 (nor_18_out, decode_1__0_31[0], decode_1__0_31_2[10]);
  nor nor_19 (nor_19_out, decode_1__0_31[2], decode_1__0_31_2[11]);
  nor nor_20 (nor_20_out, decode_1__0_31[3], decode_1__0_31_2[12]);
  nor nor_21 (nor_21_out, decode_1__0_31[4], decode_1__0_31_2[13]);
  nor nor_22 (nor_22_out, decode_1__0_31[5], decode_1__0_31_2[14]);
  nor nor_23 (nor_23_out, decode_1__0_31[6], decode_1__0_31_2[15]);
  or or_11 (or_11_out, decode_1__0_31[7], decode_1__0_31_2[16]);
  or or_12 (or_12_out, decode_1__0_31[8], decode_1__0_31_2[17]);
  or or_13 (or_13_out, decode_1__0_31[9], decode_1__0_31_2[18]);
  or or_14 (Branch[2], decode_1__0_31_2[30], decode_1__32_36[0]);
  or or_15 (Branch[3], decode_1__0_31_2[29], decode_1__0_31_2[31]);
  or or_16 (Unsigned, decode_1__0_31_2[31], decode_1__32_36[0]);
  or or_17 (or_17_out, and_1_out, and_2_out, and_3_out, and_4_out, and_5_out, and_8_out);
  Multiplexer #(.enable("false"), .width(5)) multiplexer_1 (
    .in0({5{1'b0}}), .in1(Instruction[11:7]), .out(rd), .sel(or_17_out));
  or or_18 (or_18_out, and_1_out, and_2_out, and_3_out, and_6_out, and_7_out, and_8_out);
  Multiplexer #(.enable("false"), .width(5)) multiplexer_2 (
    .in0({5{1'b0}}), .in1(Instruction[19:15]), .out(rs1), .sel(or_18_out));
  Decimal_To_Binary decimal_to_binary_1 (.Decimal({Branch[0], decode_1__0_31}), .binary(decimal_to_binary_1_binary));
  or or_19 (or_19_out, and_2_out, and_6_out, and_7_out);
  Multiplexer #(.enable("false"), .select(5)) multiplexer_3 (
    .in0(1'b0), .in1(nor_1_out), .in2(decode_1__0_31[1]), .in3(nor_2_out), .in4(or_1_out), .in5(nor_3_out),
    .in6(nor_4_out), .in7(or_2_out), .in8(nor_5_out), .in9(nor_6_out), .in10(or_3_out),
    .in11(decode_1__0_31_2[19]), .in12(decode_1__0_31[10]), .in13(decode_1__0_31[11]),
    .in14(decode_1__0_31[12]), .in15(decode_1__0_31[13]), .in16(decode_1__0_31[14]),
    .in17(decode_1__0_31[15]), .in18(decode_1__0_31[16]), .out(ALU[0]), .sel(decimal_to_binary_1_binary));  // open: in19, in20, in21, in22, in23, in24, in25, in26, in27, in28, in29, in30, in31
  Multiplexer #(.enable("false"), .select(5)) multiplexer_4 (
    .in0(1'b0), .in1(nor_7_out), .in2(decode_1__0_31[1]), .in3(or_4_out), .in4(nor_8_out), .in5(nor_9_out),
    .in6(or_5_out), .in7(or_6_out), .in8(or_7_out), .in9(nor_10_out), .in10(nor_11_out),
    .in11(decode_1__0_31_2[19]), .in12(decode_1__0_31[10]), .in13(decode_1__0_31[11]),
    .in14(decode_1__0_31[12]), .in15(decode_1__0_31[13]), .in16(decode_1__0_31[14]),
    .in17(decode_1__0_31[15]), .in18(decode_1__0_31[16]), .out(ALU[1]), .sel(decimal_to_binary_1_binary));  // open: in19, in20, in21, in22, in23, in24, in25, in26, in27, in28, in29, in30, in31
  Multiplexer #(.enable("false"), .select(5)) multiplexer_5 (
    .in0(1'b0), .in1(nor_12_out), .in2(decode_1__0_31[1]), .in3(or_8_out), .in4(or_9_out), .in5(or_10_out),
    .in6(nor_13_out), .in7(nor_14_out), .in8(nor_15_out), .in9(nor_16_out), .in10(nor_17_out),
    .in11(decode_1__0_31_2[19]), .in12(decode_1__0_31[10]), .in13(decode_1__0_31[11]),
    .in14(decode_1__0_31[12]), .in15(decode_1__0_31[13]), .in16(decode_1__0_31[14]),
    .in17(decode_1__0_31[15]), .in18(decode_1__0_31[16]), .out(ALU[2]), .sel(decimal_to_binary_1_binary));  // open: in19, in20, in21, in22, in23, in24, in25, in26, in27, in28, in29, in30, in31
  Multiplexer #(.enable("false"), .select(5)) multiplexer_6 (
    .in0(1'b0), .in1(nor_18_out), .in2(decode_1__0_31[1]), .in3(nor_19_out), .in4(nor_20_out),
    .in5(nor_21_out), .in6(nor_22_out), .in7(nor_23_out), .in8(or_11_out), .in9(or_12_out), .in10(or_13_out),
    .in11(decode_1__0_31_2[19]), .in12(decode_1__0_31[10]), .in13(decode_1__0_31[11]),
    .in14(decode_1__0_31[12]), .in15(decode_1__0_31[13]), .in16(decode_1__0_31[14]),
    .in17(decode_1__0_31[15]), .in18(decode_1__0_31[16]), .out(ALU[3]), .sel(decimal_to_binary_1_binary));  // open: in19, in20, in21, in22, in23, in24, in25, in26, in27, in28, in29, in30, in31
  or or_20 (immediate_select, decode_1__0_31_2[10], decode_1__0_31_2[11], decode_1__0_31_2[12], decode_1__0_31_2[13], decode_1__0_31_2[14], decode_1__0_31_2[15], decode_1__0_31_2[16], decode_1__0_31_2[17], decode_1__0_31_2[18], decode_1__0_31_2[19], decode_1__0_31[10], decode_1__0_31[11], decode_1__0_31[12], decode_1__0_31[13], decode_1__0_31[14], decode_1__0_31[15], decode_1__0_31[16]);
  or or_21 (Mem_write, decode_1__0_31[14], decode_1__0_31[15], decode_1__0_31[16]);
  or or_22 (WE, decode_1__0_31[0], decode_1__0_31[1], decode_1__0_31[2], decode_1__0_31[3], decode_1__0_31[4], decode_1__0_31[5], decode_1__0_31[6], decode_1__0_31[7], decode_1__0_31[8], decode_1__0_31[9], decode_1__0_31_2[10], decode_1__0_31_2[11], decode_1__0_31_2[12], decode_1__0_31_2[13], decode_1__0_31_2[14], decode_1__0_31_2[15], decode_1__0_31_2[16], decode_1__0_31_2[17], decode_1__0_31_2[18], decode_1__0_31_2[19], decode_1__0_31[10], decode_1__0_31[11], decode_1__0_31[12], decode_1__0_31[13], decode_1__32_36[1], decode_1__32_36[2], decode_1__32_36[3], decode_1__32_36[4]);
  or or_23 (ALU_WB, decode_1__0_31[0], decode_1__0_31[1], decode_1__0_31[2], decode_1__0_31[3], decode_1__0_31[4], decode_1__0_31[5], decode_1__0_31[6], decode_1__0_31[7], decode_1__0_31[8], decode_1__0_31[9], decode_1__0_31_2[10], decode_1__0_31_2[11], decode_1__0_31_2[12], decode_1__0_31_2[13], decode_1__0_31_2[14], decode_1__0_31_2[15], decode_1__0_31_2[16], decode_1__0_31_2[17], decode_1__0_31_2[18]);
  or or_24 (ID_EX_memread, decode_1__0_31_2[19], decode_1__0_31[10], decode_1__0_31[11], decode_1__0_31[12], decode_1__0_31[13]);
  or or_25 (Jump, decode_1__32_36[1], decode_1__32_36[2]);
  Multiplexer #(.enable("false"), .width(5)) multiplexer_7 (
    .in0({5{1'b0}}), .in1(Instruction[24:20]), .out(rs2), .sel(or_19_out));

  // Notes on the sheet:
  //   1000  < , 0100 >/ , 0010  != , 0001 =
endmodule

module main (
  input  CLK,
  input  CLR,
  output [31:0] out_3,
  output [31:0] out_4,
  output [3:0] out_5,
  output [1:0] out_6
);

  wire branch_1_branch, decode_signals_1_alu_wb, decode_signals_1_id_ex_memread,
       decode_signals_1_immediate_select, decode_signals_1_jump, decode_signals_1_mem_write,
       decode_signals_1_unsigned, decode_signals_1_we, ex_mem_1_alu_wb_2, ex_mem_1_branch_2,
       ex_mem_1_bubble_2, ex_mem_1_jump_2, ex_mem_1_mem_write_2, ex_mem_1_we_2, hazard_detection_1_stall,
       id_ex_1_alu_wb_2, id_ex_1_bubble, id_ex_1_immediate_select_2, id_ex_1_jump_2, id_ex_1_mem_read_2,
       id_ex_1_mem_write_2, id_ex_1_unsigned_2, id_ex_1_we_2, mem_wb_1_alu_wb_2, mem_wb_1_we_2, or_1_out;
  wire [1:0] forwarding_unit_1_a;
  wire [3:0] decode_signals_1_alu, decode_signals_1_branch, id_ex_1_branch_2;
  wire [4:0] decode_signals_1_rd, decode_signals_1_rs1, decode_signals_1_rs2, ex_mem_1_rd_2, id_ex_1_rd_2,
       id_ex_1_rs1_3, id_ex_1_rs2_3, mem_wb_1_rd_2;
  wire [23:0] bit_extender_1_out, bit_extender_2_out;
  wire [31:0] adder_1_out, adder_2_out, alu_1_result, ex_mem_1_alu_2, ex_mem_1_pc_2, ex_mem_1_write_data_2,
       id_ex_1_immediate_2, id_ex_1_pc_2, id_ex_1_rs1_4, id_ex_1_rs2_4, if_id_1_instruction_out,
       if_id_1_pc_out, imm_gen_1_output, mem_wb_1_alu_2, mem_wb_1_data_2, multiplexer_1_out,
       multiplexer_2_out, multiplexer_3_out, multiplexer_4_out, multiplexer_5_out, multiplexer_6_out,
       program_counter_1_out_5, ram_1_dout, rom_1_data;

  Multiplexer #(.enable("false"), .width(32)) multiplexer_1 (
    .in0(adder_1_out), .in1(ex_mem_1_pc_2), .out(multiplexer_1_out), .sel(or_1_out));
  Program_Counter program_counter_1 (
    .CLR(CLR), .CLK(CLK), .Data(multiplexer_1_out), .out_5(program_counter_1_out_5),
    .stall(hazard_detection_1_stall));
  ROM #(.addrWidth(24), .dataWidth(32)) rom_1 (.addr(bit_extender_1_out), .data(rom_1_data));
  Bit_Extender #(.in_width(32), .out_width(24)) bit_extender_1 (.in(program_counter_1_out_5), .out(bit_extender_1_out));
  Adder #(.width(32)) adder_1 (.a(32'h1), .b(program_counter_1_out_5), .out(adder_1_out));  // open: cin, cout
  IF_ID if_id_1 (
    .Instruction_In(rom_1_data), .PC_In(program_counter_1_out_5), .CLK(CLK), .CLR(CLR),
    .PC_Out(if_id_1_pc_out), .Stall(hazard_detection_1_stall), .Instruction_Out(if_id_1_instruction_out));
  Hazard_Detection hazard_detection_1 (
    .Instruction(if_id_1_instruction_out), .rd(id_ex_1_rd_2), .MemRead(id_ex_1_mem_read_2),
    .Stall(hazard_detection_1_stall));
  Decode_Signals decode_signals_1 (
    .Instruction(if_id_1_instruction_out), .rd(decode_signals_1_rd), .rs1(decode_signals_1_rs1),
    .rs2(decode_signals_1_rs2), .ALU(decode_signals_1_alu),
    .immediate_select(decode_signals_1_immediate_select), .Branch(decode_signals_1_branch),
    .Unsigned(decode_signals_1_unsigned), .Mem_write(decode_signals_1_mem_write), .WE(decode_signals_1_we),
    .ALU_WB(decode_signals_1_alu_wb), .ID_EX_memread(decode_signals_1_id_ex_memread),
    .Jump(decode_signals_1_jump));
  Imm_Gen imm_gen_1 (.Instruction(if_id_1_instruction_out), .Output(imm_gen_1_output));
  Register_File register_file_1 (
    .CLK(CLK), .Data_In(multiplexer_6_out), .rs1(decode_signals_1_rs1), .Select(mem_wb_1_rd_2),
    .rs2(decode_signals_1_rs2), .rs1_out(out_4), .rs2_out(out_3), .CLR(CLR), .WE(mem_wb_1_we_2));
  ID_EX id_ex_1 (
    .Immediate(imm_gen_1_output), .ALU(decode_signals_1_alu), .rd(decode_signals_1_rd), .rs1_2(out_4),
    .rs2_2(out_3), .CLk(CLK), .CLR(CLR), .immediate_2(id_ex_1_immediate_2), .ALU_2(out_5),
    .rd_2(id_ex_1_rd_2), .rs1_4(id_ex_1_rs1_4), .rs2_4(id_ex_1_rs2_4),
    .immediate_select(decode_signals_1_immediate_select), .immediate_select_2(id_ex_1_immediate_select_2),
    .PC_2(id_ex_1_pc_2), .PC(if_id_1_pc_out), .rs2(decode_signals_1_rs2), .rs1(decode_signals_1_rs1),
    .rs1_3(id_ex_1_rs1_3), .rs2_3(id_ex_1_rs2_3), .mem_write(decode_signals_1_mem_write),
    .mem_write_2(id_ex_1_mem_write_2), .WE(decode_signals_1_we), .WE_2(id_ex_1_we_2),
    .ALU_WB(decode_signals_1_alu_wb), .ALU_WB_2(id_ex_1_alu_wb_2), .mem_read(decode_signals_1_id_ex_memread),
    .mem_read_2(id_ex_1_mem_read_2), .Stall(hazard_detection_1_stall),
    .\unsigned (decode_signals_1_unsigned), .unsigned_2(id_ex_1_unsigned_2),
    .branch(decode_signals_1_branch), .branch_2(id_ex_1_branch_2), .bubble(id_ex_1_bubble),
    .Jump(decode_signals_1_jump), .Jump_2(id_ex_1_jump_2));
  Multiplexer #(.enable("false"), .select(2), .width(32)) multiplexer_2 (
    .in0(id_ex_1_rs2_4), .in1(multiplexer_6_out), .in2(ex_mem_1_alu_2), .out(multiplexer_2_out), .sel(out_6));  // open: in3
  Multiplexer #(.enable("false"), .width(32)) multiplexer_3 (
    .in0(id_ex_1_pc_2), .in1(id_ex_1_rs1_4), .out(multiplexer_3_out), .sel(id_ex_1_jump_2));
  Multiplexer #(.enable("false"), .select(2), .width(32)) multiplexer_4 (
    .in0(id_ex_1_rs1_4), .in1(multiplexer_6_out), .in2(ex_mem_1_alu_2), .out(multiplexer_4_out),
    .sel(forwarding_unit_1_a));  // open: in3
  Multiplexer #(.enable("false"), .width(32)) multiplexer_5 (
    .in0(multiplexer_2_out), .in1(id_ex_1_immediate_2), .out(multiplexer_5_out),
    .sel(id_ex_1_immediate_select_2));
  Forwarding_Unit forwarding_unit_1 (
    .rs1(id_ex_1_rs1_3), .rdmem(ex_mem_1_rd_2), .rdwb(mem_wb_1_rd_2), .rs2(id_ex_1_rs2_3),
    .regwrite_wb(mem_wb_1_we_2), .regwrite_mem(ex_mem_1_we_2), .A(forwarding_unit_1_a), .B(out_6),
    .bubble(ex_mem_1_bubble_2));
  Adder #(.width(32)) adder_2 (.a(id_ex_1_immediate_2), .b(multiplexer_3_out), .out(adder_2_out));  // open: cin, cout
  ALU alu_1 (.A(multiplexer_4_out), .B(multiplexer_5_out), .Select(out_5), .Result(alu_1_result));
  Branch branch_1 (
    .A(multiplexer_4_out), .B(id_ex_1_rs2_4), .Unsigned(id_ex_1_unsigned_2), .Select(id_ex_1_branch_2),
    .Branch(branch_1_branch));
  or or_1 (or_1_out, ex_mem_1_jump_2, ex_mem_1_branch_2);
  EX_MEM ex_mem_1 (
    .ALU(alu_1_result), .write_data(multiplexer_2_out), .PC(adder_2_out), .rd(id_ex_1_rd_2), .CLK(CLK),
    .CLR(CLR), .ALU_2(ex_mem_1_alu_2), .write_data_2(ex_mem_1_write_data_2), .PC_2(ex_mem_1_pc_2),
    .rd_2(ex_mem_1_rd_2), .mem_write(id_ex_1_mem_write_2), .mem_write_2(ex_mem_1_mem_write_2),
    .WE(id_ex_1_we_2), .WE_2(ex_mem_1_we_2), .ALU_WB(id_ex_1_alu_wb_2), .ALU_WB_2(ex_mem_1_alu_wb_2),
    .Branch(branch_1_branch), .Branch_2(ex_mem_1_branch_2), .Bubble(id_ex_1_bubble),
    .Bubble_2(ex_mem_1_bubble_2), .Jump(id_ex_1_jump_2), .Jump_2(ex_mem_1_jump_2));
  RAM #(.addrWidth(24), .dataWidth(32)) ram_1 (
    .addr(bit_extender_2_out), .we(ex_mem_1_mem_write_2), .clk(CLK), .din(ex_mem_1_write_data_2),
    .dout(ram_1_dout));
  Bit_Extender #(.in_width(32), .out_width(24)) bit_extender_2 (.in(ex_mem_1_alu_2), .out(bit_extender_2_out));
  MEM_WB mem_wb_1 (
    .Data(ram_1_dout), .ALU(ex_mem_1_alu_2), .rd(ex_mem_1_rd_2), .CLK(CLK), .CLR(CLR),
    .Data_2(mem_wb_1_data_2), .ALU_2(mem_wb_1_alu_2), .rd_2(mem_wb_1_rd_2), .WE(ex_mem_1_we_2),
    .WE_2(mem_wb_1_we_2), .ALU_WB(ex_mem_1_alu_wb_2), .ALU_WB_2(mem_wb_1_alu_wb_2));
  Multiplexer #(.enable("false"), .width(32)) multiplexer_6 (
    .in0(mem_wb_1_data_2), .in1(mem_wb_1_alu_2), .out(multiplexer_6_out), .sel(mem_wb_1_alu_wb_2));

  // Notes on the sheet:
  //   contents of rom_1 (hex, n*v repeats v):
  //   0 102083 202103 1101b3 141ce63 2f20a3 3f2123 102083 202103 1f0ee7
  //   add branch prediction
  //   fix store word/byte/half word
  //   after a stall, the last instruction in the ID stage is wiped (not good)
endmodule

module ALU (
  input  [31:0] A,
  input  [31:0] B,
  input  [3:0] Select,
  output [31:0] Result
);

  wire comparator_1_lt, comparator_2_lt;
  wire [4:0] bit_extender_1_out, bit_extender_2_out, bit_extender_3_out;
  wire [31:0] adder_1_out, and_1_out, bit_extender_4_out, bit_extender_5_out, or_1_out, shifter_1_out,
       shifter_2_out, shifter_3_out, subtractor_1_out, xor_1_out;

  Adder #(.width(32)) adder_1 (.a(A), .b(B), .out(adder_1_out));  // open: cin, cout
  Subtractor #(.width(32)) subtractor_1 (.a(A), .b(B), .out(subtractor_1_out));  // open: bin, bout
  assign and_1_out = A & B;  // AND_Gate and_1, 32 bits wide
  assign or_1_out = A | B;  // OR_Gate or_1, 32 bits wide
  assign xor_1_out = A ^ B;  // XOR_Gate xor_1, 32 bits wide
  Bit_Extender #(.in_width(32), .out_width(5)) bit_extender_1 (.in(B), .out(bit_extender_1_out));
  Shifter #(.width(32)) shifter_1 (.in(A), .\dist (bit_extender_2_out), .out(shifter_1_out));
  Bit_Extender #(.in_width(32), .out_width(5)) bit_extender_2 (.in(B), .out(bit_extender_2_out));
  Shifter #(.shift("lr"), .width(32)) shifter_2 (.in(A), .\dist (bit_extender_3_out), .out(shifter_2_out));
  Bit_Extender #(.in_width(32), .out_width(5)) bit_extender_3 (.in(B), .out(bit_extender_3_out));
  Comparator #(.width(32)) comparator_1 (.a(A), .b(B), .lt(comparator_1_lt));  // open: gt, eq
  Comparator #(.mode("unsigned"), .width(32)) comparator_2 (.a(A), .b(B), .lt(comparator_2_lt));  // open: gt, eq
  Shifter #(.shift("ar"), .width(32)) shifter_3 (.in(A), .\dist (bit_extender_1_out), .out(shifter_3_out));
  assign bit_extender_4_out = {{31{comparator_1_lt}}, comparator_1_lt};  // Bit_Extender bit_extender_4
  assign bit_extender_5_out = {{31{comparator_2_lt}}, comparator_2_lt};  // Bit_Extender bit_extender_5
  Multiplexer #(.enable("false"), .select(4), .width(32)) multiplexer_1 (
    .in0(adder_1_out), .in1(subtractor_1_out), .in2(shifter_1_out), .in3(shifter_2_out), .in4(and_1_out),
    .in5(or_1_out), .in6(xor_1_out), .in7({32{1'b0}}), .in8(bit_extender_4_out), .in9(bit_extender_5_out),
    .in10(shifter_3_out), .in11({32{1'b0}}), .in12({32{1'b0}}), .in13({32{1'b0}}), .in14({32{1'b0}}),
    .in15({32{1'b0}}), .out(Result), .sel(Select));
endmodule

module Decimal_To_Binary (
  input  [17:0] Decimal,
  output [4:0] binary
);

  wire or_1_out, or_2_out, or_3_out, or_4_out, or_5_out, or_6_out, or_7_out, or_8_out, or_9_out, or_10_out,
       or_11_out, or_12_out, or_13_out, or_14_out, or_15_out, or_16_out, or_17_out;

  or or_1 (or_1_out, Decimal[0], Decimal[1], Decimal[2], Decimal[3], Decimal[4], Decimal[5], Decimal[6], Decimal[7], Decimal[8], Decimal[9], Decimal[10], Decimal[11], Decimal[12], Decimal[13], Decimal[14], Decimal[15], Decimal[16], Decimal[17]);
  or or_2 (or_2_out, Decimal[1], Decimal[2], Decimal[3], Decimal[4], Decimal[5], Decimal[6], Decimal[7], Decimal[8], Decimal[9], Decimal[10], Decimal[11], Decimal[12], Decimal[13], Decimal[14], Decimal[15], Decimal[16], Decimal[17]);
  or or_3 (or_3_out, Decimal[2], Decimal[3], Decimal[4], Decimal[5], Decimal[6], Decimal[7], Decimal[8], Decimal[9], Decimal[10], Decimal[11], Decimal[12], Decimal[13], Decimal[14], Decimal[15], Decimal[16], Decimal[17]);
  or or_4 (or_4_out, Decimal[3], Decimal[4], Decimal[5], Decimal[6], Decimal[7], Decimal[8], Decimal[9], Decimal[10], Decimal[11], Decimal[12], Decimal[13], Decimal[14], Decimal[15], Decimal[16], Decimal[17]);
  or or_5 (or_5_out, Decimal[4], Decimal[5], Decimal[6], Decimal[7], Decimal[8], Decimal[9], Decimal[10], Decimal[11], Decimal[12], Decimal[13], Decimal[14], Decimal[15], Decimal[16], Decimal[17]);
  or or_6 (or_6_out, Decimal[5], Decimal[6], Decimal[7], Decimal[8], Decimal[9], Decimal[10], Decimal[11], Decimal[12], Decimal[13], Decimal[14], Decimal[15], Decimal[16], Decimal[17]);
  or or_7 (or_7_out, Decimal[6], Decimal[7], Decimal[8], Decimal[9], Decimal[10], Decimal[11], Decimal[12], Decimal[13], Decimal[14], Decimal[15], Decimal[16], Decimal[17]);
  or or_8 (or_8_out, Decimal[7], Decimal[8], Decimal[9], Decimal[10], Decimal[11], Decimal[12], Decimal[13], Decimal[14], Decimal[15], Decimal[16], Decimal[17]);
  or or_9 (or_9_out, Decimal[8], Decimal[9], Decimal[10], Decimal[11], Decimal[12], Decimal[13], Decimal[14], Decimal[15], Decimal[16], Decimal[17]);
  or or_10 (or_10_out, Decimal[9], Decimal[10], Decimal[11], Decimal[12], Decimal[13], Decimal[14], Decimal[15], Decimal[16], Decimal[17]);
  or or_11 (or_11_out, Decimal[10], Decimal[11], Decimal[12], Decimal[13], Decimal[14], Decimal[15], Decimal[16], Decimal[17]);
  or or_12 (or_12_out, Decimal[11], Decimal[12], Decimal[13], Decimal[14], Decimal[15], Decimal[16], Decimal[17]);
  or or_13 (or_13_out, Decimal[12], Decimal[13], Decimal[14], Decimal[15], Decimal[16], Decimal[17]);
  or or_14 (or_14_out, Decimal[13], Decimal[14], Decimal[15], Decimal[16], Decimal[17]);
  or or_15 (or_15_out, Decimal[14], Decimal[15], Decimal[16], Decimal[17]);
  or or_16 (or_16_out, Decimal[15], Decimal[16], Decimal[17]);
  or or_17 (or_17_out, Decimal[16], Decimal[17]);
  BitAdder #(.width(1)) bitadder_1 (
    .in0(or_1_out), .in1(or_2_out), .in2(or_3_out), .in3(or_4_out), .in4(or_5_out), .in5(or_6_out),
    .in6(or_7_out), .in7(or_8_out), .in8(or_9_out), .in9(or_10_out), .in10(or_11_out), .in11(or_12_out),
    .in12(or_13_out), .in13(or_14_out), .in14(or_15_out), .in15(or_16_out), .in16(or_17_out),
    .in17(Decimal[17]), .out(binary));
endmodule

module IF_ID (
  input  [31:0] Instruction_In,
  input  [31:0] PC_In,
  input  CLK,
  input  CLR,
  input  Stall,
  output [31:0] Instruction_Out,
  output [31:0] PC_Out
);

  wire not_1_out;

  not not_1 (not_1_out, Stall);
  Register #(.trigger("falling"), .width(32)) register_1 (
    .D(Instruction_In), .en(not_1_out), .clk(CLK), .Q(Instruction_Out), .clr(CLR));
  Register #(.trigger("falling"), .width(32)) register_2 (.D(PC_In), .en(not_1_out), .clk(CLK), .Q(PC_Out), .clr(CLR));
endmodule

module ID_EX (
  input  Jump,
  input  [3:0] branch,
  input  \unsigned ,
  input  mem_read,
  input  ALU_WB,
  input  WE,
  input  mem_write,
  input  [4:0] rs1,
  input  [4:0] rs2,
  input  [31:0] PC,
  input  immediate_select,
  input  [31:0] Immediate,
  input  [3:0] ALU,
  input  [4:0] rd,
  input  [31:0] rs1_2,
  input  [31:0] rs2_2,
  input  CLk,
  input  CLR,
  input  Stall,
  output Jump_2,
  output [3:0] branch_2,
  output unsigned_2,
  output mem_read_2,
  output ALU_WB_2,
  output WE_2,
  output mem_write_2,
  output [4:0] rs1_3,
  output [4:0] rs2_3,
  output [31:0] PC_2,
  output immediate_select_2,
  output [31:0] immediate_2,
  output [3:0] ALU_2,
  output [4:0] rd_2,
  output [31:0] rs1_4,
  output [31:0] rs2_4,
  output bubble
);

  wire multiplexer_1_out, multiplexer_3_out, multiplexer_4_out, multiplexer_5_out, multiplexer_6_out,
       multiplexer_7_out, multiplexer_11_out;
  wire [3:0] multiplexer_2_out, multiplexer_13_out;
  wire [4:0] multiplexer_8_out, multiplexer_9_out, multiplexer_14_out;
  wire [31:0] multiplexer_10_out, multiplexer_12_out, multiplexer_15_out, multiplexer_16_out;

  Multiplexer #(.enable("false")) multiplexer_1 (.in0(Jump), .in1(1'b0), .out(multiplexer_1_out), .sel(Stall));
  Multiplexer #(.enable("false"), .width(4)) multiplexer_2 (
    .in0(branch), .in1(4'b0000), .out(multiplexer_2_out), .sel(Stall));
  Multiplexer #(.enable("false")) multiplexer_3 (.in0(\unsigned ), .in1(1'b0), .out(multiplexer_3_out), .sel(Stall));
  Multiplexer #(.enable("false")) multiplexer_4 (.in0(mem_read), .in1(1'b0), .out(multiplexer_4_out), .sel(Stall));
  Multiplexer #(.enable("false")) multiplexer_5 (.in0(ALU_WB), .in1(1'b0), .out(multiplexer_5_out), .sel(Stall));
  Multiplexer #(.enable("false")) multiplexer_6 (.in0(WE), .in1(1'b0), .out(multiplexer_6_out), .sel(Stall));
  Multiplexer #(.enable("false")) multiplexer_7 (.in0(mem_write), .in1(1'b0), .out(multiplexer_7_out), .sel(Stall));
  Multiplexer #(.enable("false"), .width(5)) multiplexer_8 (
    .in0(rs1), .in1({5{1'b0}}), .out(multiplexer_8_out), .sel(Stall));
  Multiplexer #(.enable("false"), .width(5)) multiplexer_9 (
    .in0(rs2), .in1({5{1'b0}}), .out(multiplexer_9_out), .sel(Stall));
  Multiplexer #(.enable("false"), .width(32)) multiplexer_10 (
    .in0(PC), .in1({32{1'b0}}), .out(multiplexer_10_out), .sel(Stall));
  Multiplexer #(.enable("false")) multiplexer_11 (
    .in0(immediate_select), .in1(1'b0), .out(multiplexer_11_out), .sel(Stall));
  Multiplexer #(.enable("false"), .width(32)) multiplexer_12 (
    .in0(Immediate), .in1({32{1'b0}}), .out(multiplexer_12_out), .sel(Stall));
  Multiplexer #(.enable("false"), .width(4)) multiplexer_13 (
    .in0(ALU), .in1(4'b0000), .out(multiplexer_13_out), .sel(Stall));
  Multiplexer #(.enable("false"), .width(5)) multiplexer_14 (
    .in0(rd), .in1({5{1'b0}}), .out(multiplexer_14_out), .sel(Stall));
  Multiplexer #(.enable("false"), .width(32)) multiplexer_15 (
    .in0(rs1_2), .in1({32{1'b0}}), .out(multiplexer_15_out), .sel(Stall));
  Multiplexer #(.enable("false"), .width(32)) multiplexer_16 (
    .in0(rs2_2), .in1({32{1'b0}}), .out(multiplexer_16_out), .sel(Stall));
  Register #(.trigger("falling"), .width(1)) register_1 (
    .D(multiplexer_1_out), .en(1'b1), .clk(CLk), .Q(Jump_2), .clr(CLR));
  Register #(.trigger("falling"), .width(4)) register_2 (
    .D(multiplexer_2_out), .en(1'b1), .clk(CLk), .Q(branch_2), .clr(CLR));
  Register #(.trigger("falling"), .width(1)) register_3 (
    .D(multiplexer_3_out), .en(1'b1), .clk(CLk), .Q(unsigned_2), .clr(CLR));
  Register #(.trigger("falling"), .width(1)) register_4 (
    .D(multiplexer_4_out), .en(1'b1), .clk(CLk), .Q(mem_read_2), .clr(CLR));
  Register #(.trigger("falling"), .width(1)) register_5 (
    .D(multiplexer_5_out), .en(1'b1), .clk(CLk), .Q(ALU_WB_2), .clr(CLR));
  Register #(.trigger("falling"), .width(1)) register_6 (
    .D(multiplexer_6_out), .en(1'b1), .clk(CLk), .Q(WE_2), .clr(CLR));
  Register #(.trigger("falling"), .width(1)) register_7 (
    .D(multiplexer_7_out), .en(1'b1), .clk(CLk), .Q(mem_write_2), .clr(CLR));
  Register #(.trigger("falling"), .width(5)) register_8 (
    .D(multiplexer_8_out), .en(1'b1), .clk(CLk), .Q(rs1_3), .clr(CLR));
  Register #(.trigger("falling"), .width(5)) register_9 (
    .D(multiplexer_9_out), .en(1'b1), .clk(CLk), .Q(rs2_3), .clr(CLR));
  Register #(.trigger("falling"), .width(32)) register_10 (
    .D(multiplexer_10_out), .en(1'b1), .clk(CLk), .Q(PC_2), .clr(CLR));
  Register #(.trigger("falling"), .width(1)) register_11 (
    .D(multiplexer_11_out), .en(1'b1), .clk(CLk), .Q(immediate_select_2), .clr(CLR));
  Register #(.trigger("falling"), .width(32)) register_12 (
    .D(multiplexer_12_out), .en(1'b1), .clk(CLk), .Q(immediate_2), .clr(CLR));
  Register #(.trigger("falling"), .width(4)) register_13 (
    .D(multiplexer_13_out), .en(1'b1), .clk(CLk), .Q(ALU_2), .clr(CLR));
  Register #(.trigger("falling"), .width(5)) register_14 (
    .D(multiplexer_14_out), .en(1'b1), .clk(CLk), .Q(rd_2), .clr(CLR));
  Register #(.trigger("falling"), .width(32)) register_15 (
    .D(multiplexer_15_out), .en(1'b1), .clk(CLk), .Q(rs1_4), .clr(CLR));
  Register #(.trigger("falling"), .width(32)) register_16 (
    .D(multiplexer_16_out), .en(1'b1), .clk(CLk), .Q(rs2_4), .clr(CLR));
  Register #(.trigger("falling"), .width(1)) register_17 (.D(Stall), .en(1'b1), .clk(CLk), .Q(bubble), .clr(CLR));
endmodule

module Imm_Gen (
  input  [31:0] Instruction,
  output [31:0] Output
);

  wire and_2_out, and_4_out, and_5_out, and_7_out;
  wire [2:0] or_2_out;
  wire [31:0] bit_extender_1_out, bit_extender_2_out, bit_extender_3_out, bit_extender_4_out;

  assign bit_extender_1_out = {{20{Instruction[31]}}, Instruction[31:20]};  // Bit_Extender bit_extender_1
  assign bit_extender_2_out = {{20{Instruction[31]}}, {Instruction[31:25], Instruction[11:7]}};  // Bit_Extender bit_extender_2
  assign bit_extender_3_out = {{19{Instruction[31]}}, {Instruction[31], Instruction[7], Instruction[30:25], Instruction[11:8], 1'b0}};  // Bit_Extender bit_extender_3
  assign bit_extender_4_out = {{11{Instruction[31]}}, {Instruction[31], Instruction[19:12], Instruction[20], Instruction[30:21], 1'b0}};  // Bit_Extender bit_extender_4
  Multiplexer #(.enable("false"), .select(3), .width(32)) multiplexer_1 (
    .in0(bit_extender_1_out), .in1(bit_extender_2_out), .in2(bit_extender_3_out),
    .in3({Instruction[31:12], {12{1'b0}}}), .in4(bit_extender_4_out), .out(Output), .sel(or_2_out));  // open: in5, in6, in7
  // AND_Gate and_1 has open pins: in0=Instruction[0], in1=Instruction[1], in2=Instruction[2], in3=Instruction[3], in4=Instruction[4], in5=Instruction[5], in6=Instruction[6], out=open
  and and_2 (and_2_out, Instruction[0], Instruction[1], Instruction[2], ~Instruction[3], Instruction[4], Instruction[5], ~Instruction[6]);  // AND_Gate
  and and_3 (or_2_out[2], Instruction[0], Instruction[1], Instruction[2], Instruction[3], ~Instruction[4], Instruction[5], Instruction[6]);  // AND_Gate
  and and_4 (and_4_out, Instruction[0], Instruction[1], ~Instruction[2], ~Instruction[3], ~Instruction[4], Instruction[5], ~Instruction[6]);  // AND_Gate
  and and_5 (and_5_out, Instruction[0], Instruction[1], ~Instruction[2], ~Instruction[3], ~Instruction[4], Instruction[5], Instruction[6]);  // AND_Gate
  // AND_Gate and_6 has open pins: in0=Instruction[0], in1=Instruction[1], in2=Instruction[2], in3=Instruction[3], in4=Instruction[4], in5=Instruction[5], in6=Instruction[6], out=open
  and and_7 (and_7_out, Instruction[0], Instruction[1], Instruction[2], ~Instruction[3], Instruction[4], ~Instruction[5], ~Instruction[6]);  // AND_Gate
  or or_1 (or_2_out[1], and_5_out, and_2_out);
  or or_2 (or_2_out[0], and_2_out, and_4_out);

  // Notes on the sheet:
  //   I-type
  //   S-type
  //   B-type
  //   U-type
  //   J-type
endmodule

module Branch (
  input  [31:0] A,
  input  [31:0] B,
  input  Unsigned,
  input  [3:0] Select,
  output Branch
);

  wire comparator_1_eq, comparator_1_gt, comparator_1_lt, comparator_2_eq, comparator_2_gt, comparator_2_lt,
       multiplexer_1_out, multiplexer_2_out, not_1_out, or_1_out, or_2_out;

  Comparator #(.mode("unsigned"), .width(32)) comparator_1 (
    .a(A), .b(B), .gt(comparator_1_gt), .eq(comparator_1_eq), .lt(comparator_1_lt));
  Comparator #(.width(32)) comparator_2 (
    .a(A), .b(B), .gt(comparator_2_gt), .eq(comparator_2_eq), .lt(comparator_2_lt));
  or or_1 (or_1_out, comparator_2_gt, comparator_2_eq);
  not not_1 (not_1_out, comparator_1_eq);
  or or_2 (or_2_out, comparator_1_gt, comparator_1_eq);
  Multiplexer #(.enable("false")) multiplexer_1 (
    .in0(comparator_2_lt), .in1(comparator_1_lt), .out(multiplexer_1_out), .sel(Unsigned));
  Multiplexer #(.enable("false")) multiplexer_2 (
    .in0(or_1_out), .in1(or_2_out), .out(multiplexer_2_out), .sel(Unsigned));
  Multiplexer #(.enable("false"), .select(4)) multiplexer_3 (
    .in0(1'b0), .in1(comparator_1_eq), .in2(not_1_out), .in3(1'b0), .in4(multiplexer_2_out), .in5(1'b0),
    .in6(1'b0), .in7(1'b0), .in8(multiplexer_1_out), .in9(1'b0), .in10(1'b0), .in11(1'b0), .in12(1'b0),
    .in13(1'b0), .in14(1'b0), .in15(1'b0), .out(Branch), .sel(Select));

  // Notes on the sheet:
  //   unsigned
  //   Signed
  //   Branch_not_equal
  //   Branch_equal
  //   Branch_less
  //   Branch_greater/equal
endmodule

module Forwarding_Unit (
  input  [4:0] rs1,
  input  [4:0] rdmem,
  input  [4:0] rdwb,
  input  [4:0] rs2,
  input  regwrite_wb,
  input  regwrite_mem,
  input  bubble,
  output [1:0] A,
  output [1:0] B
);

  wire and_1_out, and_2_out, and_4_out, and_5_out, and_6_out, and_7_out, and_8_out, and_9_out, and_10_out,
       comparator_1_eq, comparator_2_eq, comparator_3_eq, comparator_4_eq, comparator_5_eq, comparator_6_eq,
       comparator_7_eq, comparator_8_eq, not_1_out, not_2_out, or_1_out, or_2_out, or_3_out;

  Comparator #(.mode("unsigned"), .width(5)) comparator_1 (
    .a(rdmem), .b({5{1'b0}}), .eq(comparator_1_eq));  // open: gt, lt
  not not_1 (not_1_out, comparator_2_eq);
  Comparator #(.mode("unsigned"), .width(5)) comparator_2 (
    .a(rdwb), .b({5{1'b0}}), .eq(comparator_2_eq));  // open: gt, lt
  Comparator #(.mode("unsigned"), .width(5)) comparator_3 (.a(rdmem), .b(rs1), .eq(comparator_3_eq));  // open: gt, lt
  not not_2 (not_2_out, comparator_1_eq);
  and and_1 (and_1_out, not_2_out, regwrite_mem);
  Comparator #(.mode("unsigned"), .width(5)) comparator_4 (.a(rs1), .b(rdwb), .eq(comparator_4_eq));  // open: gt, lt
  and and_2 (and_2_out, regwrite_wb, not_1_out);
  Comparator #(.mode("unsigned"), .width(5)) comparator_5 (.a(rdwb), .b(rs2), .eq(comparator_5_eq));  // open: gt, lt
  Comparator #(.mode("unsigned"), .width(5)) comparator_6 (
    .a(rdmem), .b({5{1'b0}}), .eq(comparator_6_eq));  // open: gt, lt
  and and_3 (A[1], comparator_3_eq, and_1_out);
  and and_4 (and_4_out, comparator_4_eq, and_2_out);
  and and_5 (and_5_out, and_2_out, comparator_5_eq);
  and and_6 (and_6_out, not_2_out, regwrite_mem);
  or or_1 (or_1_out, bubble, not_2_out);
  Comparator #(.mode("unsigned"), .width(5)) comparator_7 (.a(rdmem), .b(rs1), .eq(comparator_7_eq));  // open: gt, lt
  and and_7 (and_7_out, and_5_out, ~and_6_out);  // AND_Gate
  and and_8 (and_8_out, and_4_out, ~comparator_7_eq);  // AND_Gate
  and and_9 (and_9_out, or_1_out, or_2_out);
  or or_2 (or_2_out, bubble, regwrite_mem);
  Comparator #(.mode("unsigned"), .width(5)) comparator_8 (.a(rdmem), .b(rs2), .eq(comparator_8_eq));  // open: gt, lt
  and and_10 (and_10_out, or_1_out, regwrite_mem);
  and and_11 (A[0], and_8_out, and_9_out);
  and and_12 (B[1], comparator_8_eq, and_10_out);
  or or_3 (or_3_out, comparator_8_eq, comparator_6_eq);
  and and_13 (B[0], and_7_out, or_3_out);
endmodule

module EX_MEM (
  input  Jump,
  input  Bubble,
  input  Branch,
  input  ALU_WB,
  input  WE,
  input  mem_write,
  input  [31:0] ALU,
  input  [31:0] write_data,
  input  [31:0] PC,
  input  [4:0] rd,
  input  CLK,
  input  CLR,
  output Jump_2,
  output Bubble_2,
  output Branch_2,
  output ALU_WB_2,
  output WE_2,
  output mem_write_2,
  output [31:0] ALU_2,
  output [31:0] write_data_2,
  output [31:0] PC_2,
  output [4:0] rd_2
);

  Register #(.trigger("falling"), .width(1)) register_1 (.D(Jump), .en(1'b1), .clk(CLK), .Q(Jump_2), .clr(CLR));
  Register #(.trigger("falling"), .width(1)) register_2 (.D(Bubble), .en(1'b1), .clk(CLK), .Q(Bubble_2), .clr(CLR));
  Register #(.trigger("falling"), .width(1)) register_3 (.D(Branch), .en(1'b1), .clk(CLK), .Q(Branch_2), .clr(CLR));
  Register #(.trigger("falling"), .width(1)) register_4 (.D(ALU_WB), .en(1'b1), .clk(CLK), .Q(ALU_WB_2), .clr(CLR));
  Register #(.trigger("falling"), .width(1)) register_5 (.D(WE), .en(1'b1), .clk(CLK), .Q(WE_2), .clr(CLR));
  Register #(.trigger("falling"), .width(1)) register_6 (
    .D(mem_write), .en(1'b1), .clk(CLK), .Q(mem_write_2), .clr(CLR));
  Register #(.trigger("falling"), .width(32)) register_7 (.D(ALU), .en(1'b1), .clk(CLK), .Q(ALU_2), .clr(CLR));
  Register #(.trigger("falling"), .width(32)) register_8 (
    .D(write_data), .en(1'b1), .clk(CLK), .Q(write_data_2), .clr(CLR));
  Register #(.trigger("falling"), .width(32)) register_9 (.D(PC), .en(1'b1), .clk(CLK), .Q(PC_2), .clr(CLR));
  Register #(.trigger("falling"), .width(5)) register_10 (.D(rd), .en(1'b1), .clk(CLK), .Q(rd_2), .clr(CLR));
endmodule

module MEM_WB (
  input  ALU_WB,
  input  WE,
  input  [31:0] Data,
  input  [31:0] ALU,
  input  [4:0] rd,
  input  CLK,
  input  CLR,
  output ALU_WB_2,
  output WE_2,
  output [31:0] Data_2,
  output [31:0] ALU_2,
  output [4:0] rd_2
);

  Register #(.trigger("falling"), .width(1)) register_1 (.D(ALU_WB), .en(1'b1), .clk(CLK), .Q(ALU_WB_2), .clr(CLR));
  Register #(.trigger("falling"), .width(1)) register_2 (.D(WE), .en(1'b1), .clk(CLK), .Q(WE_2), .clr(CLR));
  Register #(.trigger("falling"), .width(32)) register_3 (.D(Data), .en(1'b1), .clk(CLK), .Q(Data_2), .clr(CLR));
  Register #(.trigger("falling"), .width(32)) register_4 (.D(ALU), .en(1'b1), .clk(CLK), .Q(ALU_2), .clr(CLR));
  Register #(.trigger("falling"), .width(5)) register_5 (.D(rd), .en(1'b1), .clk(CLK), .Q(rd_2), .clr(CLR));
endmodule

module Hazard_Detection (
  input  [31:0] Instruction,
  input  [4:0] rd,
  input  MemRead,
  output Stall
);

  wire and_1_out, and_2_out, and_3_out, and_4_out, comparator_1_eq, comparator_2_eq, comparator_3_eq,
       comparator_4_eq, comparator_5_eq, comparator_6_eq, comparator_7_eq, comparator_8_eq, comparator_9_eq,
       comparator_10_eq, comparator_11_eq, nor_1_out, not_1_out, not_2_out, or_1_out, or_2_out;

  Comparator #(.mode("unsigned"), .width(5)) comparator_1 (
    .a(Instruction[19:15]), .b(rd), .eq(comparator_1_eq));  // open: gt, lt
  Comparator #(.mode("unsigned"), .width(5)) comparator_2 (
    .a(Instruction[24:20]), .b(rd), .eq(comparator_2_eq));  // open: gt, lt
  not not_1 (not_1_out, comparator_3_eq);
  Comparator #(.mode("unsigned"), .width(32)) comparator_3 (
    .a(Instruction), .b({32{1'b0}}), .eq(comparator_3_eq));  // open: gt, lt
  not not_2 (not_2_out, comparator_4_eq);
  Comparator #(.mode("unsigned"), .width(5)) comparator_4 (
    .a(rd), .b({5{1'b0}}), .eq(comparator_4_eq));  // open: gt, lt
  Comparator #(.mode("unsigned"), .width(7)) comparator_5 (
    .a(Instruction[6:0]), .b(7'b1100011), .eq(comparator_5_eq));  // open: gt, lt
  Comparator #(.mode("unsigned"), .width(7)) comparator_6 (
    .a(Instruction[6:0]), .b(7'b0011001), .eq(comparator_6_eq));  // open: gt, lt
  Comparator #(.mode("unsigned"), .width(7)) comparator_7 (
    .a(Instruction[6:0]), .b(7'b0000011), .eq(comparator_7_eq));  // open: gt, lt
  Comparator #(.mode("unsigned"), .width(7)) comparator_8 (
    .a(Instruction[6:0]), .b(7'b0000011), .eq(comparator_8_eq));  // open: gt, lt
  Comparator #(.mode("unsigned"), .width(7)) comparator_9 (
    .a(Instruction[6:0]), .b(7'b0010001), .eq(comparator_9_eq));  // open: gt, lt
  Comparator #(.mode("unsigned"), .width(5)) comparator_10 (
    .a(Instruction[19:15]), .b(rd), .eq(comparator_10_eq));  // open: gt, lt
  Comparator #(.mode("unsigned"), .width(5)) comparator_11 (
    .a(Instruction[24:20]), .b(rd), .eq(comparator_11_eq));  // open: gt, lt
  and and_1 (and_1_out, comparator_1_eq, MemRead);
  nor nor_1 (nor_1_out, comparator_6_eq, comparator_7_eq, comparator_8_eq, comparator_9_eq);
  and and_2 (and_2_out, comparator_5_eq, or_1_out);
  or or_1 (or_1_out, comparator_10_eq, comparator_11_eq);
  and and_3 (and_3_out, comparator_2_eq, nor_1_out);
  or or_2 (or_2_out, and_1_out, and_3_out, and_2_out);
  and and_4 (and_4_out, or_2_out, not_1_out);
  and and_5 (Stall, and_4_out, not_2_out);
  Pull_Resistor pull_resistor_1 (.node(Stall));

  // Notes on the sheet:
  //   I_type opcodes
  //   Branch
  //   need jalr
  //   and U_type
endmodule

module test (
  input  mem_read,
  input  ALU_WB,
  input  WE,
  input  mem_write,
  input  [4:0] rs1,
  input  [4:0] rs2,
  input  [31:0] PC,
  input  immediate_select,
  input  [31:0] Immediate,
  input  [3:0] ALU,
  input  [4:0] rd,
  input  [31:0] rs1_2,
  input  [31:0] rs2_2,
  input  CLk,
  input  CLR,
  input  Stall,
  input  CLk_2,
  input  CLR_2,
  input  Stall_2,
  output mem_read_2,
  output ALU_WB_2,
  output WE_2,
  output mem_write_2,
  output [4:0] rs1_3,
  output [4:0] rs2_3,
  output [31:0] PC_2,
  output immediate_select_2,
  output [31:0] immediate_2,
  output [3:0] ALU_2,
  output [4:0] rd_2,
  output [31:0] rs1_4,
  output [31:0] rs2_4
);

  wire and_1_out, and_2_out, d_ff_1_q, d_ff_2_q, multiplexer_1_out, multiplexer_2_out, multiplexer_3_out,
       multiplexer_4_out, multiplexer_8_out, not_1_out, not_2_out, or_1_out, or_2_out, xor_1_out, xor_2_out;
  wire [3:0] multiplexer_10_out;
  wire [4:0] multiplexer_5_out, multiplexer_6_out, multiplexer_11_out;
  wire [31:0] multiplexer_7_out, multiplexer_9_out, multiplexer_12_out, multiplexer_13_out;

  Multiplexer #(.enable("false")) multiplexer_1 (.in0(mem_read), .in1(1'b0), .out(multiplexer_1_out), .sel(Stall_2));
  Multiplexer #(.enable("false")) multiplexer_2 (.in0(ALU_WB), .in1(1'b0), .out(multiplexer_2_out), .sel(Stall_2));
  Multiplexer #(.enable("false")) multiplexer_3 (.in0(WE), .in1(1'b0), .out(multiplexer_3_out), .sel(Stall_2));
  Multiplexer #(.enable("false")) multiplexer_4 (.in0(mem_write), .in1(1'b0), .out(multiplexer_4_out), .sel(Stall_2));
  Multiplexer #(.enable("false"), .width(5)) multiplexer_5 (
    .in0(rs1), .in1({5{1'b0}}), .out(multiplexer_5_out), .sel(Stall_2));
  Multiplexer #(.enable("false"), .width(5)) multiplexer_6 (
    .in0(rs2), .in1({5{1'b0}}), .out(multiplexer_6_out), .sel(Stall_2));
  Multiplexer #(.enable("false"), .width(32)) multiplexer_7 (
    .in0(PC), .in1({32{1'b0}}), .out(multiplexer_7_out), .sel(Stall_2));
  Multiplexer #(.enable("false")) multiplexer_8 (
    .in0(immediate_select), .in1(1'b0), .out(multiplexer_8_out), .sel(Stall_2));
  Multiplexer #(.enable("false"), .width(32)) multiplexer_9 (
    .in0(Immediate), .in1({32{1'b0}}), .out(multiplexer_9_out), .sel(Stall_2));
  Multiplexer #(.enable("false"), .width(4)) multiplexer_10 (
    .in0(ALU), .in1(4'b0000), .out(multiplexer_10_out), .sel(Stall_2));
  Multiplexer #(.enable("false"), .width(5)) multiplexer_11 (
    .in0(rd), .in1({5{1'b0}}), .out(multiplexer_11_out), .sel(Stall_2));
  Multiplexer #(.enable("false"), .width(32)) multiplexer_12 (
    .in0(rs1_2), .in1({32{1'b0}}), .out(multiplexer_12_out), .sel(Stall_2));
  Multiplexer #(.enable("false"), .width(32)) multiplexer_13 (
    .in0(rs2_2), .in1({32{1'b0}}), .out(multiplexer_13_out), .sel(Stall_2));
  Register #(.trigger("falling"), .width(1)) register_1 (
    .D(multiplexer_1_out), .en(1'b1), .clk(or_1_out), .Q(mem_read_2), .clr(CLR_2));
  Register #(.trigger("falling"), .width(1)) register_2 (
    .D(multiplexer_2_out), .en(1'b1), .clk(or_1_out), .Q(ALU_WB_2), .clr(CLR_2));
  Register #(.trigger("falling"), .width(1)) register_3 (
    .D(multiplexer_3_out), .en(1'b1), .clk(or_1_out), .Q(WE_2), .clr(CLR_2));
  Register #(.trigger("falling"), .width(1)) register_4 (
    .D(multiplexer_4_out), .en(1'b1), .clk(or_1_out), .Q(mem_write_2), .clr(CLR_2));
  Register #(.trigger("falling"), .width(5)) register_5 (
    .D(multiplexer_5_out), .en(1'b1), .clk(or_1_out), .Q(rs1_3), .clr(CLR_2));
  Register #(.trigger("falling"), .width(5)) register_6 (
    .D(multiplexer_6_out), .en(1'b1), .clk(or_1_out), .Q(rs2_3), .clr(CLR_2));
  Register #(.trigger("falling"), .width(32)) register_7 (
    .D(multiplexer_7_out), .en(1'b1), .clk(or_1_out), .Q(PC_2), .clr(CLR_2));
  Register #(.trigger("falling"), .width(1)) register_8 (
    .D(multiplexer_8_out), .en(1'b1), .clk(or_1_out), .Q(immediate_select_2), .clr(CLR_2));
  Register #(.trigger("falling"), .width(32)) register_9 (
    .D(multiplexer_9_out), .en(1'b1), .clk(or_1_out), .Q(immediate_2), .clr(CLR_2));
  Register #(.trigger("falling"), .width(4)) register_10 (
    .D(multiplexer_10_out), .en(1'b1), .clk(or_1_out), .Q(ALU_2), .clr(CLR_2));
  Register #(.trigger("falling"), .width(5)) register_11 (
    .D(multiplexer_11_out), .en(1'b1), .clk(or_1_out), .Q(rd_2), .clr(CLR_2));
  Register #(.trigger("falling"), .width(32)) register_12 (
    .D(multiplexer_12_out), .en(1'b1), .clk(or_1_out), .Q(rs1_4), .clr(CLR_2));
  Register #(.trigger("falling"), .width(32)) register_13 (
    .D(multiplexer_13_out), .en(1'b1), .clk(or_1_out), .Q(rs2_4), .clr(CLR_2));
  or or_1 (or_1_out, xor_1_out, d_ff_1_q);
  xor xor_1 (xor_1_out, CLk_2, Stall_2);
  D_Flip_Flop #(.trigger("falling")) d_ff_1 (
    .D(xor_1_out), .clk(CLk_2), .Q(d_ff_1_q), .reset(and_1_out));  // open: Qn, preset
  not not_1 (not_1_out, CLk_2);
  and and_1 (and_1_out, d_ff_1_q, not_1_out);
  Register #(.trigger("falling"), .width(32)) register_14 (.clk(or_2_out));  // open: D, en, Q, clr
  or or_2 (or_2_out, xor_2_out, d_ff_2_q);
  xor xor_2 (xor_2_out, CLk, Stall);
  D_Flip_Flop d_ff_2 (.D(Stall), .clk(CLk), .Q(d_ff_2_q), .reset(and_2_out));  // open: Qn, preset
  not not_2 (not_2_out, CLk);
  and and_2 (and_2_out, d_ff_2_q, not_2_out);
endmodule

module \new  (
  input  CLK,
  input  CLR,
  input  in_3,
  input  in_4,
  input  in_5,
  output [4:0] out_6,
  output [4:0] out_7,
  output [31:0] out_8,
  output [31:0] out_9,
  output [31:0] out_10,
  output [31:0] out_11,
  output out_12,
  output [31:0] out_13,
  output out_14
);

  wire branch_1_branch, decode_signals_1_alu_wb, decode_signals_1_id_ex_memread,
       decode_signals_1_immediate_select, decode_signals_1_mem_write, decode_signals_1_we,
       hazard_detection_1_stall, undriven_2, undriven_3, undriven_4;
  wire [3:0] decode_signals_1_alu, decode_signals_1_branch;
  wire [4:0] decode_signals_1_rs1, decode_signals_1_rs2, undriven_5;
  wire [23:0] bit_extender_1_out;
  wire [31:0] adder_1_out, if_id_1_pc_out, imm_gen_1_output, multiplexer_1_out, program_counter_1_out_5,
       undriven;

  Multiplexer #(.enable("false"), .width(32)) multiplexer_1 (
    .in0(adder_1_out), .in1(undriven), .out(multiplexer_1_out), .sel(branch_1_branch));
  Program_Counter program_counter_1 (
    .CLR(CLR), .CLK(CLK), .Data(multiplexer_1_out), .out_5(program_counter_1_out_5), .stall(undriven_2));
  ROM #(.addrWidth(24), .dataWidth(32)) rom_1 (.addr(bit_extender_1_out), .data(out_8));
  Bit_Extender #(.in_width(32), .out_width(24)) bit_extender_1 (.in(program_counter_1_out_5), .out(bit_extender_1_out));
  Adder #(.width(32)) adder_1 (.a(32'h1), .b(program_counter_1_out_5), .out(adder_1_out));  // open: cin, cout
  IF_ID if_id_1 (
    .Instruction_In(out_8), .PC_In(program_counter_1_out_5), .CLK(CLK), .CLR(CLR), .PC_Out(if_id_1_pc_out),
    .Stall(hazard_detection_1_stall), .Instruction_Out(out_9));
  Hazard_Detection hazard_detection_1 (
    .Instruction(out_9), .rd(out_7), .MemRead(undriven_3), .Stall(hazard_detection_1_stall));
  Decode_Signals decode_signals_1 (
    .Instruction(out_9), .rd(out_6), .rs1(decode_signals_1_rs1), .rs2(decode_signals_1_rs2),
    .ALU(decode_signals_1_alu), .immediate_select(decode_signals_1_immediate_select),
    .Branch(decode_signals_1_branch), .Unsigned(out_12), .Mem_write(decode_signals_1_mem_write),
    .WE(decode_signals_1_we), .ALU_WB(decode_signals_1_alu_wb), .ID_EX_memread(decode_signals_1_id_ex_memread));  // open: Jump
  Imm_Gen imm_gen_1 (.Instruction(out_9), .Output(imm_gen_1_output));
  Register_File register_file_1 (
    .CLK(CLK), .Data_In(out_13), .rs1(decode_signals_1_rs1), .Select(undriven_5), .rs2(decode_signals_1_rs2),
    .rs1_out(out_10), .rs2_out(out_11), .CLR(CLR), .WE(undriven_4));
  Branch branch_1 (
    .A(out_10), .B(out_11), .Unsigned(out_12), .Select(decode_signals_1_branch), .Branch(branch_1_branch));
  // test test_1: pin names not known; wires that end beside it: in_3, in_4, in_5, out_14

  // Notes on the sheet:
  //   contents of rom_1 (hex, n*v repeats v):
  //   0 300103 2100a3 400083 208233
  //   check the noop insertion into ID/EX
endmodule
